# Fritzing sketch Radio-Circuit-00 (saved by Fritzing 0.8.5b)
breadboards: 1

parts:
  U1 = MIC [package=mic_electret_smd]
  R1 = Resistor [tolerance=±5% resistance=3.9k package=THT]
  U3 = LIPO-1000mAh [package=lipo-1000]
  R2 = Resistor [tolerance=±5% resistance=3.9k package=THT]
  IC1 = Dual Op-Amp [package=dip08]
  R3 = Resistor [tolerance=±5% resistance=100k package=THT]
  R4 = Resistor [tolerance=±5% resistance=100k package=THT]
  R5 = Resistor [tolerance=±5% resistance=3.3k package=THT]
  R6 = Resistor [tolerance=±5% resistance=150k package=THT]
  C1 = Electrolytic Capacitor [capacitance=1000μF package="1010 [SMD, electrolytic]"]
  IC3 = Dual Op-Amp [package=dip08]

nets:
  N1: U1.1, U3.-, IC1.A_V-, R3.Pin_1, R4.Pin_1, IC3.Ground
  N2: U1.2, R1.Pin_1
  N3: R1.Pin_0, R2.Pin_1, C1.+
  N4: U3.+, R2.Pin_0, IC1.A_V+
  N5: IC1.A_OUT, IC1.A_-IN, R5.Pin_1
  N6: IC1.A_+IN, R3.Pin_0, R4.Pin_0
  N7: IC1.B_+IN, C1.-
  N8: IC1.B_-IN, R5.Pin_0, R6.Pin_1
  N9: IC1.B_OUT, R6.Pin_0, IC3.Signal

notes:
  This is an AM Transmitter which sends voice through the airwaves. Just tune radio to 1000 AM.
  -------------------------------------------
  designed by G. S. Kielian under MIT License 2014
  Connect this wire to any larger metal object to improve the transmitter range.

custom parts:
  Dual Op-Amp: Generic op-amp footprint
