# Fritzing sketch LED-Light-06-Night-Light (saved by Fritzing 0.8.5b)
breadboards: 1

parts:
  LED4 = LED - 5mm [color="Red (635nm)" package="5 mm [THT]"]
  BAT1 = Battery Holders [package=battcom_20mm_pth]
  Q1 = NPN-Transistor [part_number=2n2222 package="TO92 [THT]"]
  R1 = PHOTOCELL [package=photocell-kit]
  R3 = Resistor [tolerance=±5% resistance=4.7k package=THT]

nets:
  N1: LED4.cathode, BAT1.+, R1.P$1
  N2: LED4.anode, Q1.E
  N3: BAT1.-, Q1.C, R3.Pin_0
  N4: Q1.B, R1.P$2, R3.Pin_1
