# Fritzing sketch LED-Light-07-Dimmer-Switch (saved by Fritzing 0.8.5b)
breadboards: 1

parts:
  LED4 = LED - 5mm [color="Red (635nm)" package="5 mm [THT]"]
  BAT1 = Battery Holders [package=battcom_20mm_pth]
  R1 = Rotary Potentiometer (Small) [maximum_resistance=100kΩ package=THT]
  R2 = Resistor [tolerance=±5% resistance=20 package=THT]
  U1 = SWITCH_SPDT [package=kps-1290]

nets:
  N1: LED4.cathode, BAT1.-
  N2: LED4.anode, R2.Pin_0
  N3: BAT1.+, U1.P
  N4: R1.leg1, R2.Pin_1
  N5: R1.wiper, U1.O
