# Fritzing sketch LED-Light-09-Red-Light-Green-Light (saved by Fritzing 0.8.5b)
breadboards: 1

parts:
  LED4 = LED - 5mm [color="Red (635nm)" package="5 mm [THT]"]
  BAT1 = Battery Holders [package=battcom_20mm_pth]
  U1 = SWITCH_SPDT [package=kps-1290]
  LED5 = LED - 5mm [color="Green (560nm)" package="5 mm [THT]"]

nets:
  N1: LED4.cathode, BAT1.-, LED5.cathode
  N2: LED4.anode, U1.O
  N3: BAT1.+, U1.P
  N4: U1.S, LED5.anode
