# Fritzing sketch MIC-Amp-01 (saved by Fritzing 0.8.5b)
breadboards: 1

parts:
  BAT1 = Battery Holders [package=battcom_20mm_pth]
  U5 = MIC [package=mic-9.7mm]
  IC1 = Dual Op-Amp [package=dip08]
  R1 = Resistor [tolerance=±5% resistance=4.7k package=THT]
  C1 = Ceramic Capacitor [capacitance=4.7µF package="200 mil [THT, multilayer]"]
  R2 = Resistor [tolerance=±5% resistance=10k package=THT]
  R3 = Resistor [tolerance=±5% resistance=100k package=THT]
  C2 = Ceramic Capacitor [capacitance=4.7µF package="200 mil [THT, multilayer]"]
  R4 = Resistor [tolerance=±5% resistance=4.7k package=THT]
  R5 = Resistor [tolerance=±5% resistance=4.7k package=THT]

nets:
  N1: BAT1.+, IC1.A_V+, R1.Pin_1, R4.Pin_0
  N2: BAT1.-, IC1.A_V-, R5.Pin_0
  N3: U5.1, R1.Pin_0
  N4: U5.2, C1.0
  N5: IC1.A_OUT, R3.Pin_0, C2.1
  N6: IC1.A_-IN, R2.Pin_1, R3.Pin_1
  N7: IC1.A_+IN, R4.Pin_1, R5.Pin_1

notes:
  Green and purple go to speaker.
