# Fritzing sketch LED-Light-2-v2 (saved by Fritzing 0.8.5b)
breadboards: 1

parts:
  LED4 = LED - 5mm [color="Red (635nm)" package="5 mm [THT]"]
  BAT1 = Battery Holders [package=battcom_20mm_pth]

nets:
  N1: LED4.cathode, BAT1.-
  N2: LED4.anode, BAT1.+
